# Fritzing sketch Sound_Sensor_PCB (saved by Fritzing 0.8.3b)
circuit board: 16.9333cm x 5.64444cm
breadboards: 1

parts:
  Componente1 = Arduino Uno (Rev3)
  U1 = RELAY [package=relay-jzc]
  Componente2 = Breakout Board for Electret Microphone

nets:
  N1: Componente1.A0, Componente2.AUD
  5V: Componente1.5V, U1.MAIN, Componente2.VCC
  GND: Componente1.GND, U1.COIL1, Componente2.GND
  N2: Componente1.D4, U1.COIL2
